# Fritzing sketch AutoWatering-NewBoard (saved by Fritzing 0.9.9b)
breadboards: 1

parts:
  IC1 = MCP23017 I2C I/O Expander
  U1 = 74HC595 [package="DIP16 [THT]"]
  U11 = JST XH 5A
  U12 = JST XH 5A
  C5 = Electrolytic Capacitor [capacitance=100μF voltage=16V package="0807 [SMD, electrolytic]"]
  C6 = Ceramic Capacitor [capacitance=100nF voltage=35V package="200 mil [THT, multilayer]"]
  U14 = JST XH 3A Male [chip_label=? package=THT]
  U15 = JST XH 3A Male [chip_label=? package=THT]
  U16 = JST XH 3A Male [chip_label=? package=THT]
  U17 = JST XH 3A Male [chip_label=? package=THT]
  U18 = JST XH 3A Male [chip_label=? package=THT]
  U19 = JST XH 3A Male [chip_label=? package=THT]
  J1 = female pin header, 4 pins [form="♀ (female)"]
  J2 = female pin header, 3 pins [form="♀ (female)"]
  J3 = female pin header, 3 pins [form="♀ (female)"]
  J4 = female pin header, 3 pins [form="♀ (female)"]
  J5 = male pin header, 6 pins [form="♂ (male)"]
  J6 = male pin header, 1 pin [form="♂ (male)"]
  C8 = Ceramic Capacitor [capacitance=10nF voltage=35V package="200 mil [THT, multilayer]"]
  R1 = Resistor [tolerance=±5% resistance=10k package="0603 [SMD]"]

nets:
  N1: IC1.GPB0, U14.pin2
  N2: IC1.GPB1, U15.pin2
  N3: IC1.GPB2, U16.pin2
  N4: IC1.GPB3, U17.pin2
  N5: IC1.GPB4, U18.pin2
  N6: IC1.GPB5, U19.pin2
  N7: IC1.GPB6, J5.pin6
  N8: IC1.GPB7, U1.Q6, R1.Pin_1
  VDD: IC1.VDD, IC1.VSS, C5.-, C6.0, C6.1, U14.pin3, U15.pin3, U16.pin3, U17.pin3, U19.pin3, R1.Pin_0
  N9: IC1.SCL, U11.pin1, U12.pin1
  N10: IC1.SDA, U11.pin2, U12.pin2
  N11: IC1.A0, J3.pin3
  N12: IC1.A1, J3.pin2
  N13: IC1.A2, J3.pin1
  N14: IC1.RESET, U1.VCC, J2.pin2, J2.pin3
  N15: IC1.GPA0, U1.SH_CP
  N16: IC1.GPA1, U1.MR
  N17: IC1.GPA2, U1.Q7'
  N18: IC1.GPA3, J5.pin1
  N19: IC1.GPA4, J5.pin2
  N20: IC1.GPA5, J5.pin3
  N21: IC1.GPA6, J5.pin4
  N22: IC1.GPA7, J5.pin5
  N23: U1.Q1, U18.pin1
  N24: U1.Q3, U11.pin3, U12.pin3
  N25: U1.Q5, U19.pin1
  N26: U1.ST_CP, U17.pin1
  N27: U1.OE, U14.pin1
  N28: U1.DS, U15.pin1
  N29: U1.Q0, U16.pin1
  N30: U11.pin4, U12.pin4
  N31: U11.pin5, U12.pin5
  N32: J1.pin2, J4.pin2, J4.pin3, J6.pin1, C8.0

custom parts:
  MCP23017 I2C I/O Expander: The MCP23017 uses two i2c pins (these can be shared with other i2c devices), and in exchange gives you 16 general purpose pins. You can set each of 16 pins to be input, output, input with a pullup or open drain. There's even the ability to get an interrupt via an external pin when any of the inputs change so you don't have to keep polling the chip.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
  JST XH 5A: JST XH 5A 2.54.mm
  JST XH 3A Male: 2.54 Mm JST "XH" connector
