# Fritzing sketch Autowatering (saved by Fritzing 0.9.10b)
breadboards: 1

parts:
  M1 = Arduino NANO RP2040 CONNECT with headers
  Part4 = ULN2803 Darlington Array
  IC2 = MCP23017 I2C I/O Expander
  Part1 = Dollatek 2.4' SPI Touchscreen TFT 320x240 [package=1x11_smd_no_holes]
  R1 = Resistor [tolerance=±5% power=0.25 resistance=10k package=THT]
  R5 = Resistor [tolerance=±5% power=0.25 resistance=10k package=THT]
  Part3 = 74HC4051 breakout
  R6 = Resistor [tolerance=±5% power=0.25 resistance=2.2M package=THT]
  R7 = Resistor [tolerance=±5% power=0.25 resistance=2.2M package=THT]
  R8 = Resistor [tolerance=±5% power=0.25 resistance=2.2M package=THT]
  R9 = Resistor [tolerance=±5% power=0.25 resistance=2.2M package=THT]
  Part5 = Soil Moisture Sensor  # not connected
  M2 = DC Motor [voltage_(max)=6V voltage_(min)=3V]
  J6 = JST XH 2A male [form="♂ (male)" package=THT]
  J7 = JST XH 2A male [form="♂ (male)" package=THT]
  U1 = JST XH 3A Male [chip_label=? package=THT]
  U2 = JST XH 3A Male [chip_label=? package=THT]
  J8 = JST XH 2A male [form="♂ (male)" package=THT]
  J9 = JST XH 2A male [form="♂ (male)" package=THT]
  U3 = JST XH 3A Male [chip_label=? package=THT]
  J10 = Power Jack [package=power_jack_smd]
  DHT1 = DHT22 Humidity and Temperature Sensor  # not connected
  U8 = JST XH 3A Male [chip_label=? package=THT]
  U10 = JST XH 5A
  U11 = JST XH 5A
  R11 = Resistor [tolerance=±5% power=0.25 resistance=10k package=THT]
  U13 = JST XH 3A Male [chip_label=? package=THT]
  R12 = Resistor [tolerance=±5% power=0.25 resistance=10k package=THT]
  C1 = Electrolytic Capacitor [capacitance=10μF voltage=50V package="0605 [SMD, electrolytic]"]
  J11 = JST XH 2A male [form="♂ (male)" package=THT]  # not connected
  J12 = JST XH 2A male [form="♂ (male)" package=THT]  # not connected
  J13 = JST XH 2A male [form="♂ (male)" package=THT]  # not connected

nets:
  N1: M1.RESET-3, Part1.RES
  N2: M1.GND-4, M1.+5V, M1.GND-29, U11.pin4
  N3: M1.D2, Part1.CS2
  N4: M1.D3, Part1.PEN
  N5: M1.D4, Part1.BLK
  N6: M1.D9, Part1.DC
  N7: M1.D10, Part1.CS1
  N8: M1.D11, Part1.MOSI
  N9: M1.D12, Part1.MISO
  N10: M1.D13, Part1.CLK
  N11: M1.+3V3, U11.pin5
  N12: M1.D17, U11.pin3
  N13: M1.D18, U11.pin2
  N14: M1.D19, U11.pin1
  N15: Part4.1B, IC2.GPA0
  N16: Part4.2B, IC2.GPA1
  GND: Part4.GND, Part4.COM, IC2.VSS, IC2.A0, IC2.A1, IC2.A2, Part1.GND, Part3.GND#2, R6.Pin_0, R7.Pin_0, R8.Pin_0, R9.Pin_0, M2.pin_1, J6.pin2, J7.pin2, U1.pin3, U2.pin3, J8.pin2, J9.pin2, U3.pin3, J10.GND, J10.GNDBREAK, U8.pin3, U10.pin4, U13.pin3, C1.-
  N17: Part4.1C, M2.pin_2, J7.pin1
  N18: Part4.2C, J6.pin1
  N19: Part4.3C, J8.pin1
  N20: Part4.4C, J9.pin1
  N21: IC2.GPB0, Part3.S0
  N22: IC2.GPB1, Part3.S1
  N23: IC2.GPB2, Part3.S2
  N24: IC2.GPB3, U2.pin2
  N25: IC2.GPB4, U1.pin2
  N26: IC2.GPB5, U3.pin2
  N27: IC2.GPB6, U13.pin2
  N28: IC2.GPB7, U8.pin2
  VDD: IC2.VDD, Part1.VCC, R1.Pin_1, R5.Pin_1, Part3.VCC#1, U10.pin5, R11.Pin_1, R12.Pin_1, C1.+
  N29: IC2.SCL, U10.pin1, R12.Pin_0
  N30: IC2.SDA, R1.Pin_0, U10.pin2
  N31: IC2.RESET, R5.Pin_0
  N32: Part3.Z, U10.pin3
  N33: Part3.Y0, R9.Pin_1, U2.pin1
  N34: Part3.Y1, R8.Pin_1, U1.pin1
  N35: Part3.Y2, R7.Pin_1, U3.pin1
  N36: Part3.Y3, R6.Pin_1, U13.pin1
  N37: Part3.Y4, U8.pin1, R11.Pin_0

notes:
  4.7k-10k pullup resistor needed for the i2c lines
  Resistors from the data pin to GND.
  Individual so we can swap them depending on moisture sensors used.
  DHT22 needs a 10k pullup resistor
  Power supply for the motors

custom parts:
  Arduino NANO RP2040 CONNECT with headers: Meet the only connected RP2040 board. It fits the Arduino Nano form factor, making it a small board with BIG features. The brain of the board is the Raspberry Pi RP2040 silicon; a dual-core Arm Cortex M0+ running at 133MHz. It has 264KB of SRAM, and the 16MB of flash memory is off-chip to give you extra storage. But what’s really exciting is the on-board connectivity options. The hugely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
  ULN2803 Darlington Array: ULN2803 Darlington Transistor Array with Flyback Protection
  MCP23017 I2C I/O Expander: The MCP23017 uses two i2c pins (these can be shared with other i2c devices), and in exchange gives you 16 general purpose pins. You can set each of 16 pins to be input, output, input with a pullup or open drain. There's even the ability to get an interrupt via an external pin when any of the inputs change so you don't have to keep polling the chip.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
  Dollatek 2.4' SPI Touchscreen TFT 320x240: For the Arduino RP2040 Connect, I had sucess using this with: * For display: Adafruit_ILI9341 (https://github.com/adafruit/Adafruit_ILI9341) + Adafruit_GFX * For touchscreen: https://github.com/PaulStoffregen/XPT2046_Touchscreen
  74HC4051 breakout: 8:1 analog mux https://learn.sparkfun.com/tutorials/multiplexer-breakout-hookup-guide/74hc4051-breakout-overview Notes: * E pin is pulled low on the breakout board via a 10k resistor. If the project doesn't require enabling/disabling the mux, the pin can be left unused
  JST XH 2A male: JST XH-2A
  JST XH 3A Male: 2.54 Mm JST "XH" connector
  JST XH 5A: JST XH 5A 2.54.mm
