# Fritzing sketch Pico-MQTTUI-Mosfets (saved by Fritzing 0.9.10b)
stripboards: 1
perfboards: 1

parts:
  Mod1 = Raspberry Pi Pico  # not connected
  J9 = Generic female header - 6 pins [form="♀ (female)" package=THT]
  J11 = Generic female header - 4 pins [form="♀ (female)" package=THT]  # not connected
  J12 = female pin header, 20 pins [form="♀ (female)"]
  J13 = female pin header, 20 pins [form="♀ (female)"]
  J14 = female pin header, 3 pins [form="♀ (female)"]

nets:
  N1: J9.GND#0, J12.pin18, J13.pin18, J14.pin1
  N2: J9.DONE, J13.pin16
  N3: J12.pin3, J13.pin3
  N4: J12.pin8, J13.pin8
  N5: J12.pin13, J13.pin13
  N6: J13.pin19, J14.pin2
  N7: J13.pin20, J14.pin3

notes:
  3 pins for UART logging, if not using USB
  SparkFun Nano Power Timer module

custom parts:
  Raspberry Pi Pico: Raspberry Pi Pico. Based around the RP2040 microcontroller the Pico is a low cost microcontroller device bringing Raspberry Pi quality, cost, and easy of use to the microcontroller space. Jan 2021, Split part in to two versions: SMD (this one) and tht. This one is single sided and uses the castellation pads to solder the module to the board (no holes, other than for the USB connector!). The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
  Generic female header - 6 pins: Generic female header
  Generic female header - 4 pins: Generic female header
