# Fritzing sketch Pico-TouchUI-I2C-Boards (saved by Fritzing 0.9.10b)
stripboards: 1
perfboards: 1

parts:
  Part2 = Dollatek 2.4' SPI Touchscreen TFT 320x240 [package=1x11_smd_no_holes]
  Mod1 = Raspberry Pi Pico
  U1 = IC, DIP package, 8 pins [chip_label=24C256]
  J2 = Generic female header - 11 pins [form="♀ (female)" package=THT]
  S1 = Toggle Switch [package=THT]
  U11 = JST XH 5A
  U12 = JST XH 5A
  U13 = JST XH 5A
  R1 = Resistor [tolerance=±5% power=0.25 resistance=4.7k package=THT]
  J9 = Generic female header - 6 pins [form="♀ (female)" package=THT]
  J11 = Generic female header - 4 pins [form="♀ (female)" package=THT]
  R2 = Resistor [tolerance=±5% power=0.25 resistance=4.7k package=THT]
  J12 = female pin header, 20 pins [form="♀ (female)"]
  J13 = female pin header, 20 pins [form="♀ (female)"]
  R3 = Resistor [tolerance=±5% power=0.25 resistance=270k package=THT]
  R4 = Resistor [tolerance=±5% power=0.25 resistance=470k package=THT]
  S2 = Toggle Switch [package=THT]

nets:
  GND: Part2.GND, Mod1.pin_3, Mod1.pin_8, Mod1.pin_13, Mod1.pin_18, Mod1.pin_23, Mod1.pin_28, Mod1.pin_33, Mod1.pin_38, U1.pin1, U1.pin2, U1.pin4, U1.pin7, J2.GND, S1.L1, U11.pin2, U12.pin2, U13.pin2, J9.GND#0, J11.GND, J12.pin3, J12.pin8, J12.pin13, J12.pin18, J13.pin3, J13.pin8, J13.pin13, J13.pin18, R4.Pin_1
  VCC: Part2.VCC, J2.VCC
  N1: Part2.CLK, Mod1.pin_9, J2.CLK, J12.pin9
  N2: Part2.MOSI, Mod1.pin_10, J2.MOSI, J12.pin10
  N3: Part2.RES, Mod1.pin_11, J2.RES, J12.pin11
  N4: Part2.DC, Mod1.pin_12, J2.DC, J12.pin12
  N5: Part2.BLK, Mod1.pin_14, J2.BLK, J12.pin14
  N6: Part2.MISO, Mod1.pin_6, J2.MISO, J12.pin6
  N7: Part2.CS1, Mod1.pin_15, J2.CS1, J12.pin15
  N8: Part2.CS2, Mod1.pin_16, J2.CS2, J12.pin16
  N9: Part2.PEN, Mod1.pin_17, J2.PEN, J12.pin17
  N10: Mod1.pin_1, U1.pin5, U11.pin4, U12.pin4, U13.pin4, J11.SDA, R2.Pin_0, J12.pin1
  N11: Mod1.pin_2, U1.pin6, U11.pin3, U12.pin3, U13.pin3, R1.Pin_0, J11.SCL, J12.pin2
  N12: Mod1.pin_4, J12.pin4
  N13: Mod1.pin_5, J12.pin5
  N14: Mod1.pin_7, J12.pin7
  N15: Mod1.pin_19, J12.pin19
  N16: Mod1.pin_20, J12.pin20
  N17: Mod1.pin_21, J13.pin20
  N18: Mod1.pin_22, J13.pin19
  N19: Mod1.pin_24, J13.pin17
  N20: Mod1.pin_25, J9.DONE, J13.pin16
  N21: Mod1.pin_26, J13.pin15
  N22: Mod1.pin_27, J13.pin14
  N23: Mod1.pin_29, J13.pin12
  N24: Mod1.pin_30, J13.pin11
  N25: Mod1.pin_31, J13.pin10, R3.Pin_0, R4.Pin_0
  N26: Mod1.pin_32, J13.pin9
  N27: Mod1.pin_34, U11.pin5, U12.pin5, U13.pin5, J13.pin7
  N28: Mod1.pin_35, J13.pin6
  N29: Mod1.pin_36, U1.pin8, U11.pin1, U12.pin1, U13.pin1, R1.Pin_1, J11.3.3V, R2.Pin_1, J13.pin5, S2.L1, S2.COM, S2.L2
  N30: Mod1.pin_37, S1.COM, J13.pin4
  N31: Mod1.pin_39, J9.VOUT, J13.pin2, R3.Pin_1
  N32: Mod1.pin_40, J13.pin1

custom parts:
  Dollatek 2.4' SPI Touchscreen TFT 320x240: For the Arduino RP2040 Connect, I had sucess using this with: * For display: Adafruit_ILI9341 (https://github.com/adafruit/Adafruit_ILI9341) + Adafruit_GFX * For touchscreen: https://github.com/PaulStoffregen/XPT2046_Touchscreen
  Raspberry Pi Pico: Raspberry Pi Pico. Based around the RP2040 microcontroller the Pico is a low cost microcontroller device bringing Raspberry Pi quality, cost, and easy of use to the microcontroller space. Jan 2021, Split part in to two versions: SMD (this one) and tht. This one is single sided and uses the castellation pads to solder the module to the board (no holes, other than for the USB connector!). The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
  Generic female header - 11 pins: Generic female header
  JST XH 5A: JST XH 5A 2.54.mm
  Generic female header - 6 pins: Generic female header
  Generic female header - 4 pins: Generic female header
